# Fritzing sketch Diagram (saved by Fritzing 0.9.3b)

parts:
  Raspberry_Pi_1 = Raspberry Pi 3 [part_number=RPI-3-V1.2]
  KY-1 = Keyes Relay [package=THT]

nets:
  N1: Raspberry_Pi_1.GIPO17, KY-1.power
  N2: Raspberry_Pi_1.GND, KY-1.ground
  N3: Raspberry_Pi_1.5V, KY-1.signal

custom parts:
  Keyes Relay: The Keyes 5V relay module is suitable for SCM development, home appliance control. It uses a 5V~12V TIL control signal which can control DC / AC signal.
